# Fritzing sketch SmartHouseRemoteESP (saved by Fritzing 0.9.3b)
circuit board: 8.46667cm x 5.64444cm
perfboards: 1

parts:
  U1 = TLP621 [package=THT]
  R2 = Resistor [tolerance=±5% resistance=10k package=THT]
  Q2 = NPN-Transistor [package="TO92 [THT]"]
  R1 = Resistor [tolerance=±5% resistance=100 package=THT]
  Q1 = NPN-Transistor [package="TO92 [THT]"]
  C1 = Electrolytic Capacitor [capacitance=100µF voltage=16V package="100 mil [THT, electrolytic]"]
  U3 = ESP8266-07 [part_number=ESP8266]
  YwRobot_Power_Supply1 = YwRobot Breadboard Power Supply [part_number=545043]
  U2 = TLP621 [package=THT]
  R4 = Resistor [tolerance=±5% resistance=10k package=THT]
  J2 = Generic male header - 11 pins-modified [form="♂ (male)" package=THT]

nets:
  N1: U1.Pin_1, R1.Pin_1, U2.Pin_1
  N2: U1.Pin_2, Q1.C
  N3: U1.Pin_4, J2.pin1
  N4: U1.Pin_3, J2.pin3
  N5: R2.Pin_0, U3.GPIO_4
  N6: R2.Pin_1, Q1.B
  N7: Q2.E, Q1.E, U3.GND
  N8: Q2.B, R4.Pin_1
  N9: Q2.C, U2.Pin_2
  N10: R1.Pin_0, C1.+, U3.VCC, YwRobot_Power_Supply1.VCC#5
  N11: C1.-, YwRobot_Power_Supply1.GND#11
  N12: U3.GPIO_5, R4.Pin_0
  N13: U2.Pin_4, J2.pin11
  N14: U2.Pin_3, J2.pin9

custom parts:
  ESP8266-07: ESP8266 - 07 WiFi Module on PCB
  YwRobot Breadboard Power Supply: The YwRobot Breadboard Power Supply (MB-V2) has two power rails; they can be 5V or 3V3. Power to the module can be provided through the female USB socket or through the A10 (female) 2.1mm power jack.
  Generic male header - 11 pins-modified: Modified Generic male header

// code stored in the sketch: SmartHomeRemote.ino

